// Digital circuit Addierer8bit.dig as structural Verilog
module Addierer8bit (
  input  [7:0] B,
  input  [7:0] A,
  output [7:0] COUT
);

  wire voll_addierer_1_cout, voll_addierer_2_cout, voll_addierer_3_cout, voll_addierer_4_cout,
       voll_addierer_5_cout, voll_addierer_6_cout, voll_addierer_7_cout;

  voll_addierer voll_addierer_1 (.A(B[0]), .B(A[0]), .CIN(1'b0), .S(COUT[0]), .COUT(voll_addierer_1_cout));
  voll_addierer voll_addierer_2 (
    .A(B[1]), .B(A[1]), .CIN(voll_addierer_1_cout), .S(COUT[1]), .COUT(voll_addierer_2_cout));
  voll_addierer voll_addierer_3 (
    .A(B[2]), .B(A[2]), .CIN(voll_addierer_2_cout), .S(COUT[2]), .COUT(voll_addierer_3_cout));
  voll_addierer voll_addierer_4 (
    .A(B[3]), .B(A[3]), .CIN(voll_addierer_3_cout), .S(COUT[3]), .COUT(voll_addierer_4_cout));
  voll_addierer voll_addierer_5 (
    .A(B[4]), .B(A[4]), .CIN(voll_addierer_4_cout), .S(COUT[4]), .COUT(voll_addierer_5_cout));
  voll_addierer voll_addierer_6 (
    .A(B[5]), .B(A[5]), .CIN(voll_addierer_5_cout), .S(COUT[5]), .COUT(voll_addierer_6_cout));
  voll_addierer voll_addierer_7 (
    .A(B[6]), .B(A[6]), .CIN(voll_addierer_6_cout), .S(COUT[6]), .COUT(voll_addierer_7_cout));
  voll_addierer voll_addierer_8 (.A(B[7]), .B(A[7]), .CIN(voll_addierer_7_cout), .S(COUT[7]));  // open: COUT
endmodule
