// Digital circuit ROM8bit.dig as structural Verilog
module ROM8bit (
  input  in_2,
  input  in_4,
  input  in_6,
  input  in_7,
  input  in_8,
  input  in_9,
  input  in_10,
  input  in_11,
  input  in_12,
  input  in_13,
  output [7:0] out_1,
  output [7:0] out_3,
  output [7:0] out_5
);

  wire and_gate_1_out, and_gate_2_out, and_gate_3_out, and_gate_4_out, and_gate_5_out, and_gate_6_out,
       and_gate_7_out, and_gate_8_out, and_gate_9_out, and_gate_10_out, and_gate_11_out, and_gate_12_out,
       and_gate_13_out, and_gate_14_out, and_gate_15_out, and_gate_16_out, and_gate_17_out, and_gate_18_out,
       and_gate_19_out, and_gate_20_out, and_gate_21_out, and_gate_22_out, and_gate_23_out, and_gate_24_out,
       and_gate_25_out, and_gate_26_out, and_gate_27_out, and_gate_28_out, and_gate_29_out, and_gate_30_out,
       and_gate_31_out, and_gate_32_out, and_gate_33_out, and_gate_34_out, and_gate_35_out, and_gate_36_out,
       and_gate_37_out, and_gate_38_out, and_gate_39_out, and_gate_40_out, and_gate_41_out, and_gate_42_out,
       not_gate_1_out, not_gate_2_out, not_gate_3_out, not_gate_4_out, not_gate_5_out, not_gate_6_out,
       not_gate_7_out, not_gate_8_out, not_gate_9_out, not_gate_10_out, not_gate_11_out, not_gate_12_out,
       not_gate_13_out, not_gate_14_out, not_gate_15_out, not_gate_16_out, not_gate_17_out, not_gate_18_out,
       not_gate_19_out, not_gate_20_out, not_gate_21_out, not_gate_22_out, not_gate_23_out, not_gate_24_out,
       not_gate_25_out, not_gate_26_out, not_gate_27_out, not_gate_28_out, not_gate_29_out, not_gate_30_out,
       not_gate_31_out, not_gate_32_out, not_gate_33_out, not_gate_34_out, not_gate_35_out, not_gate_36_out,
       not_gate_37_out, not_gate_38_out, not_gate_39_out, not_gate_40_out, not_gate_41_out, not_gate_42_out,
       not_gate_43_out, not_gate_44_out, or_gate_1_out, or_gate_2_out, or_gate_3_out, or_gate_4_out,
       or_gate_5_out, or_gate_6_out, or_gate_7_out, or_gate_8_out;
  wire [7:0] lookuptable_1_out, program_counter_1_out, rom_1_d;

  Multiplexer #(.Selector_Bits(3), .Bits(8)) multiplexer_1 (
    .sel(3'b001), .in_0(8'h1), .in_1(8'h5), .in_2(8'h1), .in_3(8'h20), .in_4(8'h7), .in_5(8'h2),
    .in_6(8'h17), .in_7(8'h18), .out(out_1));
  program_counter program_counter_1 (.Clk(in_2), .Out(program_counter_1_out));
  ROM #(.AddrBits(8), .Bits(8)) rom_1 (.A(program_counter_1_out), .sel(1'b1), .D(rom_1_d));
  Register #(.Bits(8)) register_1 (.D(rom_1_d), .C(in_2), .en(1'b1), .Q(out_3));
  Register8bit register8bit_1 (.Clk(in_4), .D0({in_13, in_9, in_12, in_8, in_11, in_7, in_10, in_6}), .Out(out_5));
  not_gate not_gate_1 (.A(1'b0), .Out(not_gate_1_out));
  not_gate not_gate_2 (.A(1'b0), .Out(not_gate_2_out));
  not_gate not_gate_3 (.A(1'b1), .Out(not_gate_3_out));
  not_gate not_gate_4 (.A(1'b0), .Out(not_gate_4_out));
  not_gate not_gate_5 (.A(1'b0), .Out(not_gate_5_out));
  not_gate not_gate_6 (.A(1'b0), .Out(not_gate_6_out));
  not_gate not_gate_7 (.A(1'b0), .Out(not_gate_7_out));
  not_gate not_gate_8 (.A(1'b0), .Out(not_gate_8_out));
  not_gate not_gate_9 (.A(1'b0), .Out(not_gate_9_out));
  not_gate not_gate_10 (.A(1'b0), .Out(not_gate_10_out));
  not_gate not_gate_11 (.A(1'b0), .Out(not_gate_11_out));
  not_gate not_gate_12 (.A(1'b0), .Out(not_gate_12_out));
  not_gate not_gate_13 (.A(1'b0), .Out(not_gate_13_out));
  not_gate not_gate_14 (.A(1'b0), .Out(not_gate_14_out));
  not_gate not_gate_15 (.A(1'b0), .Out(not_gate_15_out));
  not_gate not_gate_16 (.A(1'b0), .Out(not_gate_16_out));
  not_gate not_gate_17 (.A(1'b0), .Out(not_gate_17_out));
  not_gate not_gate_18 (.A(1'b0), .Out(not_gate_18_out));
  not_gate not_gate_19 (.A(1'b0), .Out(not_gate_19_out));
  not_gate not_gate_20 (.A(1'b0), .Out(not_gate_20_out));
  not_gate not_gate_21 (.A(1'b0), .Out(not_gate_21_out));
  not_gate not_gate_22 (.A(1'b0), .Out(not_gate_22_out));
  and_gate and_gate_1 (.A(not_gate_1_out), .B(not_gate_2_out), .Out(and_gate_1_out));
  and_gate and_gate_2 (.A(1'b1), .B(not_gate_9_out), .Out(and_gate_2_out));
  and_gate and_gate_3 (.A(not_gate_16_out), .B(1'b1), .Out(and_gate_3_out));
  and_gate and_gate_4 (.A(and_gate_1_out), .B(not_gate_3_out), .Out(and_gate_4_out));
  and_gate and_gate_5 (.A(and_gate_2_out), .B(not_gate_10_out), .Out(and_gate_5_out));
  and_gate and_gate_6 (.A(and_gate_3_out), .B(not_gate_17_out), .Out(and_gate_6_out));
  and_gate and_gate_7 (.A(and_gate_4_out), .B(not_gate_4_out), .Out(and_gate_7_out));
  and_gate and_gate_8 (.A(and_gate_5_out), .B(not_gate_11_out), .Out(and_gate_8_out));
  and_gate and_gate_9 (.A(and_gate_6_out), .B(not_gate_18_out), .Out(and_gate_9_out));
  and_gate and_gate_10 (.A(and_gate_7_out), .B(not_gate_5_out), .Out(and_gate_10_out));
  and_gate and_gate_11 (.A(and_gate_8_out), .B(not_gate_12_out), .Out(and_gate_11_out));
  and_gate and_gate_12 (.A(and_gate_9_out), .B(not_gate_19_out), .Out(and_gate_12_out));
  and_gate and_gate_13 (.A(and_gate_10_out), .B(not_gate_6_out), .Out(and_gate_13_out));
  and_gate and_gate_14 (.A(and_gate_11_out), .B(not_gate_13_out), .Out(and_gate_14_out));
  and_gate and_gate_15 (.A(and_gate_12_out), .B(not_gate_20_out), .Out(and_gate_15_out));
  and_gate and_gate_16 (.A(and_gate_13_out), .B(not_gate_7_out), .Out(and_gate_16_out));
  and_gate and_gate_17 (.A(and_gate_14_out), .B(not_gate_14_out), .Out(and_gate_17_out));
  and_gate and_gate_18 (.A(and_gate_15_out), .B(not_gate_21_out), .Out(and_gate_18_out));
  and_gate and_gate_19 (.A(and_gate_16_out), .B(not_gate_8_out), .Out(and_gate_19_out));
  and_gate and_gate_20 (.A(and_gate_17_out), .B(not_gate_15_out), .Out(and_gate_20_out));
  and_gate and_gate_21 (.A(and_gate_18_out), .B(not_gate_22_out), .Out(and_gate_21_out));
  or_gate or_gate_1 (.a(and_gate_19_out), .b(and_gate_21_out), .out(or_gate_1_out));
  or_gate or_gate_2 (.a(and_gate_20_out), .b(1'b0), .out(or_gate_2_out));
  or_gate or_gate_3 (.a(and_gate_21_out), .b(1'b0), .out(or_gate_3_out));
  or_gate or_gate_4 (.a(1'b0), .b(1'b0), .out(or_gate_4_out));
  or_gate or_gate_5 (.a(and_gate_19_out), .b(1'b0), .out(or_gate_5_out));
  or_gate or_gate_6 (.a(1'b0), .b(1'b0), .out(or_gate_6_out));
  or_gate or_gate_7 (.a(1'b0), .b(1'b0), .out(or_gate_7_out));
  or_gate or_gate_8 (.a(1'b0), .b(1'b0), .out(or_gate_8_out));
  not_gate not_gate_23 (.A(1'b0), .Out(not_gate_23_out));
  not_gate not_gate_24 (.A(1'b0), .Out(not_gate_24_out));
  not_gate not_gate_25 (.A(1'b1), .Out(not_gate_25_out));
  not_gate not_gate_26 (.A(1'b0), .Out(not_gate_26_out));
  not_gate not_gate_27 (.A(1'b0), .Out(not_gate_27_out));
  not_gate not_gate_28 (.A(1'b0), .Out(not_gate_28_out));
  not_gate not_gate_29 (.A(1'b0), .Out(not_gate_29_out));
  not_gate not_gate_30 (.A(1'b0), .Out(not_gate_30_out));
  not_gate not_gate_31 (.A(1'b0), .Out(not_gate_31_out));
  not_gate not_gate_32 (.A(1'b0), .Out(not_gate_32_out));
  not_gate not_gate_33 (.A(1'b0), .Out(not_gate_33_out));
  not_gate not_gate_34 (.A(1'b0), .Out(not_gate_34_out));
  not_gate not_gate_35 (.A(1'b0), .Out(not_gate_35_out));
  not_gate not_gate_36 (.A(1'b0), .Out(not_gate_36_out));
  not_gate not_gate_37 (.A(1'b0), .Out(not_gate_37_out));
  not_gate not_gate_38 (.A(1'b0), .Out(not_gate_38_out));
  not_gate not_gate_39 (.A(1'b1), .Out(not_gate_39_out));
  not_gate not_gate_40 (.A(1'b0), .Out(not_gate_40_out));
  not_gate not_gate_41 (.A(1'b0), .Out(not_gate_41_out));
  not_gate not_gate_42 (.A(1'b0), .Out(not_gate_42_out));
  not_gate not_gate_43 (.A(1'b0), .Out(not_gate_43_out));
  not_gate not_gate_44 (.A(1'b0), .Out(not_gate_44_out));
  and_gate and_gate_22 (.A(not_gate_23_out), .B(not_gate_24_out), .Out(and_gate_22_out));
  and_gate and_gate_23 (.A(1'b1), .B(not_gate_31_out), .Out(and_gate_23_out));
  and_gate and_gate_24 (.A(not_gate_38_out), .B(1'b0), .Out(and_gate_24_out));
  and_gate and_gate_25 (.A(and_gate_22_out), .B(not_gate_25_out), .Out(and_gate_25_out));
  and_gate and_gate_26 (.A(and_gate_23_out), .B(not_gate_32_out), .Out(and_gate_26_out));
  and_gate and_gate_27 (.A(and_gate_24_out), .B(not_gate_39_out), .Out(and_gate_27_out));
  and_gate and_gate_28 (.A(and_gate_25_out), .B(not_gate_26_out), .Out(and_gate_28_out));
  and_gate and_gate_29 (.A(and_gate_26_out), .B(not_gate_33_out), .Out(and_gate_29_out));
  and_gate and_gate_30 (.A(and_gate_27_out), .B(not_gate_40_out), .Out(and_gate_30_out));
  and_gate and_gate_31 (.A(and_gate_28_out), .B(not_gate_27_out), .Out(and_gate_31_out));
  and_gate and_gate_32 (.A(and_gate_29_out), .B(not_gate_34_out), .Out(and_gate_32_out));
  and_gate and_gate_33 (.A(and_gate_30_out), .B(not_gate_41_out), .Out(and_gate_33_out));
  and_gate and_gate_34 (.A(and_gate_31_out), .B(not_gate_28_out), .Out(and_gate_34_out));
  and_gate and_gate_35 (.A(and_gate_32_out), .B(not_gate_35_out), .Out(and_gate_35_out));
  and_gate and_gate_36 (.A(and_gate_33_out), .B(not_gate_42_out), .Out(and_gate_36_out));
  and_gate and_gate_37 (.A(and_gate_34_out), .B(not_gate_29_out), .Out(and_gate_37_out));
  and_gate and_gate_38 (.A(and_gate_35_out), .B(not_gate_36_out), .Out(and_gate_38_out));
  and_gate and_gate_39 (.A(and_gate_36_out), .B(not_gate_43_out), .Out(and_gate_39_out));
  and_gate and_gate_40 (.A(and_gate_37_out), .B(not_gate_30_out), .Out(and_gate_40_out));
  and_gate and_gate_41 (.A(and_gate_38_out), .B(not_gate_37_out), .Out(and_gate_41_out));
  and_gate and_gate_42 (.A(and_gate_39_out), .B(not_gate_44_out), .Out(and_gate_42_out));
  LookUpTable #(.Bits(8)) lookuptable_1 (
    .in0(and_gate_40_out), .in1(and_gate_41_out), .in2(and_gate_42_out), .out(lookuptable_1_out));

  // Notes on the sheet:
  //   contents of rom_1 (hex, n*v repeats v):
  //   6,254*0,5
  //   contents of lookuptable_1 (hex, n*v repeats v):
  //   5,6,7,8,2,3,4,1
endmodule
