// Digital circuit Register8bit.dig as structural Verilog
module Register8bit (
  input  Clk,
  input  [7:0] D0,
  output [7:0] Out
);

  d_flip_flop d_flip_flop_1 (.Data(D0[0]), .Clock(Clk), .Out(Out[0]));
  d_flip_flop d_flip_flop_2 (.Data(D0[1]), .Clock(Clk), .Out(Out[1]));
  d_flip_flop d_flip_flop_3 (.Data(D0[2]), .Clock(Clk), .Out(Out[2]));
  d_flip_flop d_flip_flop_4 (.Data(D0[3]), .Clock(Clk), .Out(Out[3]));
  d_flip_flop d_flip_flop_5 (.Data(D0[4]), .Clock(Clk), .Out(Out[4]));
  d_flip_flop d_flip_flop_6 (.Data(D0[5]), .Clock(Clk), .Out(Out[5]));
  d_flip_flop d_flip_flop_7 (.Data(D0[6]), .Clock(Clk), .Out(Out[6]));
  d_flip_flop d_flip_flop_8 (.Data(D0[7]), .Clock(Clk), .Out(Out[7]));
endmodule
