// Digital circuit and_gate.dig as structural Verilog
module and_gate (
  input  A,
  input  B,
  output Out
);

  wire nand_1_out, nand_2_out;

  nand nand_1 (nand_1_out, A, B);
  nand nand_2 (nand_2_out, A, B);
  nand nand_3 (Out, nand_1_out, nand_2_out);
endmodule
