// Digital circuit d_flip_flop.dig as structural Verilog
module d_flip_flop (
  input  Data,
  input  Clock,
  output Out
);

  wire latch_curcuit_1_out, not_1_out;

  latch_curcuit latch_curcuit_1 (.Data(Data), .Clock(Clock), .Out(latch_curcuit_1_out));
  not not_1 (not_1_out, Clock);
  latch_curcuit latch_curcuit_2 (.Data(latch_curcuit_1_out), .Clock(not_1_out), .Out(Out));
endmodule
