// Digital circuit d_flip_flop_8bit.dig as structural Verilog
module d_flip_flop_8bit (
  input  in_1,
  input  in_2,
  output out_3
);

  wire nand_1_out, nand_2_out, nand_4_out, not_1_out;

  nand nand_1 (nand_1_out, in_1, in_2);
  not not_1 (not_1_out, in_1);
  nand nand_2 (nand_2_out, not_1_out, in_2);
  nand nand_3 (out_3, nand_1_out, nand_4_out);
  nand nand_4 (nand_4_out, out_3, nand_2_out);
endmodule
