// Digital circuit latch_curcuit.dig as structural Verilog
module latch_curcuit (
  input  Data,
  input  Clock,
  output Out
);

  wire nand_1_out, nand_2_out, nand_4_out, not_1_out;

  nand nand_1 (nand_1_out, Data, Clock);
  not not_1 (not_1_out, Data);
  nand nand_2 (nand_2_out, not_1_out, Clock);
  nand nand_3 (Out, nand_1_out, nand_4_out);
  nand nand_4 (nand_4_out, Out, nand_2_out);
endmodule
