// Digital circuit or_gate.dig as structural Verilog
module or_gate (
  input  a,
  input  b,
  output out_3
);

  wire nand_1_out, nand_2_out;

  nand nand_1 (nand_1_out, a, a);
  nand nand_2 (nand_2_out, b, b);
  nand nand_3 (out_3, nand_1_out, nand_2_out);
endmodule
