// Digital circuit program_counter.dig as structural Verilog
module program_counter (
  input  Clk,
  output [7:0] Out
);

  wire [7:0] register8bit_1_out;

  Register8bit register8bit_1 (.Clk(Clk), .D0(Out), .Out(register8bit_1_out));
  Addierer8bit addierer8bit_1 (.B(register8bit_1_out), .A(8'h1), .COUT(Out));
endmodule
